// Logisim project 74LS373_8_bit_register.circ as structural Verilog: 1 circuit, main circuit DM74LS373
module DM74LS373 (
  input  CLK,
  input  Enable,
  input  OC,
  input  D1,
  input  D2,
  input  D3,
  input  D4,
  input  D5,
  input  D6,
  input  D7,
  input  D8,
  output Q1,
  output Q2,
  output Q3,
  output Q4,
  output Q5,
  output Q6,
  output Q7,
  output Q8
);

  wire and_1_out, and_2_out, and_3_out, and_4_out, and_5_out, and_6_out, and_7_out, and_8_out, d_ff_1_q,
       d_ff_2_q, d_ff_3_q, d_ff_4_q, d_ff_5_q, d_ff_6_q, d_ff_7_q, d_ff_8_q;

  and and_1 (and_1_out, CLK, Enable);
  and and_2 (and_2_out, CLK, Enable);
  and and_3 (and_3_out, CLK, Enable);
  and and_4 (and_4_out, CLK, Enable);
  and and_5 (and_5_out, CLK, Enable);
  and and_6 (and_6_out, CLK, Enable);
  and and_7 (and_7_out, CLK, Enable);
  and and_8 (and_8_out, CLK, Enable);
  D_Flip_Flop d_ff_1 (.D(D1), .clk(and_1_out), .Q(d_ff_1_q));  // open: Qn, preset, reset
  D_Flip_Flop d_ff_2 (.D(D2), .clk(and_3_out), .Q(d_ff_2_q));  // open: Qn, preset, reset
  D_Flip_Flop d_ff_3 (.D(D3), .clk(and_2_out), .Q(d_ff_3_q));  // open: Qn, preset, reset
  D_Flip_Flop d_ff_4 (.D(D4), .clk(and_4_out), .Q(d_ff_4_q));  // open: Qn, preset, reset
  D_Flip_Flop d_ff_5 (.D(D5), .clk(and_5_out), .Q(d_ff_5_q));  // open: Qn, preset, reset
  D_Flip_Flop d_ff_6 (.D(D6), .clk(and_6_out), .Q(d_ff_6_q));  // open: Qn, preset, reset
  D_Flip_Flop d_ff_7 (.D(D7), .clk(and_7_out), .Q(d_ff_7_q));  // open: Qn, preset, reset
  D_Flip_Flop d_ff_8 (.D(D8), .clk(and_8_out), .Q(d_ff_8_q));  // open: Qn, preset, reset
  assign Q1 = OC ? d_ff_1_q : 1'bz;  // Controlled_Buffer controlled_buffer_1
  assign Q2 = OC ? d_ff_2_q : 1'bz;  // Controlled_Buffer controlled_buffer_2
  assign Q3 = OC ? d_ff_3_q : 1'bz;  // Controlled_Buffer controlled_buffer_3
  assign Q4 = OC ? d_ff_4_q : 1'bz;  // Controlled_Buffer controlled_buffer_4
  assign Q5 = OC ? d_ff_5_q : 1'bz;  // Controlled_Buffer controlled_buffer_5
  assign Q7 = OC ? d_ff_7_q : 1'bz;  // Controlled_Buffer controlled_buffer_6
  assign Q6 = OC ? d_ff_6_q : 1'bz;  // Controlled_Buffer controlled_buffer_7
  assign Q8 = OC ? d_ff_8_q : 1'bz;  // Controlled_Buffer controlled_buffer_8
  LED led_1 (.in(Q1));
  LED led_2 (.in(Q2));
  LED led_3 (.in(Q3));
  LED led_4 (.in(Q4));
  LED led_5 (.in(Q5));
  LED led_6 (.in(Q6));
  LED led_7 (.in(Q7));
  LED led_8 (.in(Q8));

  // Other names for the same wires on the sheet: CLOCK = CLK; OUTCONTROL = OC
endmodule
