// Logisim project CD4008_4_bit_adder.circ as structural Verilog: 3 circuits, main circuit CD4008
module CD4008test (
);

  CD4008 cd4008_1 ();  // open: Ci, A1, B1, A2, B2, A3, B3, A4, B4, S1, S2, S3, S4, Co
  CD4008 cd4008_2 ();  // open: Ci, A1, B1, A2, B2, A3, B3, A4, B4, S1, S2, S3, S4, Co
endmodule

module CD4008 (
  input  Ci,
  input  A1,
  input  B1,
  input  A2,
  input  B2,
  input  A3,
  input  B3,
  input  A4,
  input  B4,
  output S1,
  output S2,
  output S3,
  output S4,
  output Co
);

  wire C0, C1, C2;

  TwoBitAdder twobitadder_1 (.A(A1), .B(B1), .C(Ci), .S(S1), .Cout(C0));
  TwoBitAdder twobitadder_2 (.A(A2), .B(B2), .C(C0), .S(S2), .Cout(C1));
  TwoBitAdder twobitadder_3 (.A(A3), .B(B3), .C(C1), .S(S3), .Cout(C2));
  TwoBitAdder twobitadder_4 (.A(A4), .B(B4), .C(C2), .S(S4), .Cout(Co));
endmodule

module TwoBitAdder (
  input  A,
  input  B,
  input  C,
  output S,
  output Cout
);

  wire and_1_out, and_2_out, xor_1_out;

  xor xor_1 (xor_1_out, A, B);
  and and_1 (and_1_out, C, xor_1_out);
  and and_2 (and_2_out, B, A);
  xor xor_2 (S, xor_1_out, C);
  or or_1 (Cout, and_1_out, and_2_out);
endmodule
