// Logisim project CD4028_BCD_TO_DECIMEL_CONV.circ as structural Verilog: 1 circuit, main circuit CD4028B
module CD4028B (
  input  A,
  input  B,
  input  C,
  input  D,
  output O0,
  output O1,
  output O2,
  output O3,
  output O4,
  output O5,
  output O6,
  output O7,
  output O8,
  output O9
);

  wire not_1_out, not_2_out, not_3_out, not_4_out, not_5_out, not_6_out, not_7_out, not_8_out, not_9_out,
       not_10_out, not_11_out, not_12_out, not_13_out, not_14_out, not_15_out, not_16_out, not_17_out,
       not_18_out, not_19_out, not_20_out, not_21_out, not_22_out, not_23_out, not_24_out, not_25_out;

  not not_1 (not_1_out, B);
  not not_2 (not_2_out, C);
  not not_3 (not_3_out, D);
  not not_4 (not_4_out, B);
  not not_5 (not_5_out, C);
  not not_6 (not_6_out, D);
  not not_7 (not_7_out, A);
  not not_8 (not_8_out, C);
  not not_9 (not_9_out, D);
  not not_10 (not_10_out, C);
  not not_11 (not_11_out, D);
  not not_12 (not_12_out, A);
  not not_13 (not_13_out, B);
  not not_14 (not_14_out, D);
  not not_15 (not_15_out, B);
  not not_16 (not_16_out, D);
  not not_17 (not_17_out, A);
  not not_18 (not_18_out, D);
  not not_19 (not_19_out, D);
  not not_20 (not_20_out, A);
  not not_21 (not_21_out, B);
  not not_22 (not_22_out, C);
  not not_23 (not_23_out, B);
  not not_24 (not_24_out, C);
  not not_25 (not_25_out, A);
  and A1 (O0, not_25_out, not_1_out, not_2_out, not_3_out);
  and A2 (O1, A, not_4_out, not_5_out, not_6_out);
  and A3 (O2, not_7_out, B, not_8_out, not_9_out);
  and A4 (O3, A, B, not_10_out, not_11_out);
  and A5 (O4, not_12_out, not_13_out, C, not_14_out);
  and A6 (O5, A, not_15_out, C, not_16_out);
  and A7 (O6, not_17_out, B, C, not_18_out);
  and A8 (O7, A, B, C, not_19_out);
  and A9 (O8, not_20_out, not_21_out, not_22_out, D);
  and A10 (O9, A, not_23_out, not_24_out, D);

  // Other names for the same wires on the sheet: T1 = A; T2 = B; T3 = C; T4 = D
endmodule
