// Logisim project CD4051.circ as structural Verilog: 1 circuit, main circuit CB4051B
module CB4051B (
  input  COM,
  input  A,
  input  B,
  input  C,
  input  INH,
  output CH0,
  output CH1,
  output CH2,
  output CH3,
  output CH4,
  output CH5,
  output CH6,
  output CH7
);

  wire A_t, and_1_out, and_2_out, and_3_out, and_4_out, and_5_out, and_6_out, and_7_out, and_8_out, B_t, C_t,
       not_1_out, NotA, NotB, NotC;

  assign A_t = not_1_out ? A : 1'bz;  // Controlled_Buffer controlled_buffer_1
  assign B_t = not_1_out ? B : 1'bz;  // Controlled_Buffer controlled_buffer_2
  assign C_t = not_1_out ? C : 1'bz;  // Controlled_Buffer controlled_buffer_3
  not not_1 (not_1_out, INH);
  not not_2 (NotA, A_t);
  not not_3 (NotB, B_t);
  not not_4 (NotC, C_t);
  and and_1 (and_1_out, NotA, NotB, NotC);
  and and_2 (and_2_out, A_t, NotB, NotC);
  and and_3 (and_3_out, NotA, B_t, NotC);
  // Transmission_Gate transmission_1: pin names not known; wires that end beside it: and_3_out, COM, CH2, 1'b0
  and and_4 (and_4_out, NotC, A_t, B_t);
  and and_5 (and_5_out, NotB, NotA, C_t);
  // Transmission_Gate transmission_2: pin names not known; wires that end beside it: and_5_out, COM, CH4, 1'b0
  and and_6 (and_6_out, A_t, NotB, C_t);
  and and_7 (and_7_out, NotA, B_t, C_t);
  and and_8 (and_8_out, A_t, B_t, C_t);
  // Transmission_Gate transmission_3: pin names not known; wires that end beside it: B_t, and_8_out, COM, CH7, 1'b0
  // Transmission_Gate transmission_4: pin names not known; wires that end beside it: and_1_out, COM, COM, CH0, 1'b0
  // Transmission_Gate transmission_5: pin names not known; wires that end beside it: and_2_out, COM, CH1, 1'b0
  // Transmission_Gate transmission_6: pin names not known; wires that end beside it: and_4_out, COM, CH3, 1'b0
  // Transmission_Gate transmission_7: pin names not known; wires that end beside it: and_6_out, COM, CH5, 1'b0
  // Transmission_Gate transmission_8: pin names not known; wires that end beside it: and_7_out, COM, CH6, 1'b0

  // Other names for the same wires on the sheet: INPT = COM

  // Notes on the sheet:
  //   CHAN0
  //   CHAN1
  //   CHAN2
  //   CHAN3
  //   CHAN4
  //   CHAN5
  //   CHAN6
  //   CHAN7
endmodule
