// Logisim project CD4094B_shiftNstore.circ as structural Verilog: 4 circuits, main circuit DflipFlop
module DflipFlop (
  input  READ,
  input  WRITE,
  input  data,
  input  clk,
  output mem
);

  wire and_1_out, d_ff_1_q;

  and and_1 (and_1_out, WRITE, clk);
  D_Flip_Flop d_ff_1 (.D(data), .clk(and_1_out), .Q(d_ff_1_q));  // open: Qn, preset, reset
  and and_2 (mem, READ, d_ff_1_q);
endmodule

module Latch_w_strobe (
  input  data,
  input  strobe,
  output Q,
  output Qinv
);

  wire RST, transmission_1_p3, TRinv;

  // Transmission_Gate transmission_1: pin names not known; wires that end beside it: strobe, data, transmission_1_p3, TRinv, Qinv
  S_R_Flip_Flop #(.trigger("high")) s_r_ff_1 (
    .S(transmission_1_p3), .R(RST), .clk(strobe), .Q(Q), .Qn(Qinv));  // open: reset, preset
  LED led_1 (.in(transmission_1_p3));
  not not_1 (TRinv, strobe);
  not not_2 (RST, transmission_1_p3);
  LED led_2 (.in(Q));
  LED led_3 (.in(Qinv));
  LED led_4 (.in(RST));

  // Other names for the same wires on the sheet: TR = strobe
endmodule

module CD4094B (
  input  STROBE,
  input  OutputEnable,
  input  DATAIN,
  input  CLOCK,
  output Q1,
  output Q2,
  output Q3,
  output Q4,
  output Q5,
  output Q6,
  output Q7,
  output Q8,
  output QS,
  output QSinv
);

  wire dflipflopsinglecellmemory_1_p4, dflipflopsinglecellmemory_2_p2, dflipflopsinglecellmemory_2_p4,
       dflipflopsinglecellmemory_3_p2, dflipflopsinglecellmemory_3_p4, dflipflopsinglecellmemory_4_p3,
       dflipflopsinglecellmemory_4_p4, dflipflopsinglecellmemory_7_p1, latch_w_strobe_1_q,
       latch_w_strobe_2_q, latch_w_strobe_3_q, latch_w_strobe_4_q, latch_w_strobe_5_q, latch_w_strobe_6_q,
       latch_w_strobe_7_q;

  // DFlipFlopSingleCellMemory dflipflopsinglecellmemory_1: pin names not known; wires that end beside it: 1'b1, DATAIN, CLOCK, dflipflopsinglecellmemory_1_p4, 1'b1, dflipflopsinglecellmemory_1_p4, CLOCK
  // DFlipFlopSingleCellMemory dflipflopsinglecellmemory_2: pin names not known; wires that end beside it: 1'b1, dflipflopsinglecellmemory_2_p2, CLOCK, dflipflopsinglecellmemory_2_p4, 1'b1, dflipflopsinglecellmemory_2_p4, CLOCK
  // DFlipFlopSingleCellMemory dflipflopsinglecellmemory_3: pin names not known; wires that end beside it: 1'b1, dflipflopsinglecellmemory_3_p2, CLOCK, dflipflopsinglecellmemory_3_p4, 1'b1, dflipflopsinglecellmemory_3_p4, CLOCK
  // DFlipFlopSingleCellMemory dflipflopsinglecellmemory_4: pin names not known; wires that end beside it: 1'b1, CLOCK, dflipflopsinglecellmemory_4_p3, dflipflopsinglecellmemory_4_p4, 1'b1, dflipflopsinglecellmemory_4_p4, CLOCK, 1'b1
  // DFlipFlopSingleCellMemory dflipflopsinglecellmemory_5: pin names not known; wires that end beside it: dflipflopsinglecellmemory_3_p2
  // DFlipFlopSingleCellMemory dflipflopsinglecellmemory_6: pin names not known; wires that end beside it: dflipflopsinglecellmemory_4_p3
  // DFlipFlopSingleCellMemory dflipflopsinglecellmemory_7: pin names not known; wires that end beside it: dflipflopsinglecellmemory_7_p1
  // DFlipFlopSingleCellMemory dflipflopsinglecellmemory_8: pin names not known; wires that end beside it: dflipflopsinglecellmemory_2_p2
  Latch_w_strobe latch_w_strobe_1 (
    .data(dflipflopsinglecellmemory_1_p4), .strobe(STROBE), .Q(latch_w_strobe_1_q));  // open: Qinv
  Latch_w_strobe latch_w_strobe_2 (
    .data(dflipflopsinglecellmemory_2_p2), .strobe(STROBE), .Q(latch_w_strobe_2_q));  // open: Qinv
  Latch_w_strobe latch_w_strobe_3 (
    .data(dflipflopsinglecellmemory_2_p4), .strobe(STROBE), .Q(latch_w_strobe_3_q));  // open: Qinv
  Latch_w_strobe latch_w_strobe_4 (
    .data(dflipflopsinglecellmemory_3_p2), .strobe(STROBE), .Q(latch_w_strobe_4_q));  // open: Qinv
  Latch_w_strobe latch_w_strobe_5 (
    .data(dflipflopsinglecellmemory_3_p4), .strobe(STROBE), .Q(latch_w_strobe_5_q));  // open: Qinv
  Latch_w_strobe latch_w_strobe_6 (
    .data(dflipflopsinglecellmemory_4_p3), .strobe(STROBE), .Q(latch_w_strobe_6_q));  // open: Qinv
  Latch_w_strobe latch_w_strobe_7 (
    .data(dflipflopsinglecellmemory_4_p4), .strobe(STROBE), .Q(latch_w_strobe_7_q));  // open: Qinv
  Latch_w_strobe latch_w_strobe_8 (.data(dflipflopsinglecellmemory_7_p1), .strobe(STROBE), .Q(QS));  // open: Qinv
  assign Q1 = OutputEnable ? latch_w_strobe_1_q : 1'bz;  // Controlled_Buffer controlled_buffer_1
  assign Q2 = OutputEnable ? latch_w_strobe_2_q : 1'bz;  // Controlled_Buffer controlled_buffer_2
  assign Q3 = OutputEnable ? latch_w_strobe_3_q : 1'bz;  // Controlled_Buffer controlled_buffer_3
  assign Q4 = OutputEnable ? latch_w_strobe_4_q : 1'bz;  // Controlled_Buffer controlled_buffer_4
  assign Q5 = OutputEnable ? latch_w_strobe_5_q : 1'bz;  // Controlled_Buffer controlled_buffer_5
  assign Q6 = OutputEnable ? latch_w_strobe_6_q : 1'bz;  // Controlled_Buffer controlled_buffer_6
  assign Q7 = OutputEnable ? latch_w_strobe_7_q : 1'bz;  // Controlled_Buffer controlled_buffer_7
  assign Q8 = OutputEnable ? QS : 1'bz;  // Controlled_Buffer controlled_buffer_8
  not not_1 (QSinv, QS);

  // Other names for the same wires on the sheet: CLK = CLOCK; OE = OutputEnable; STB = STROBE
endmodule

module CD4094TEST (
  input  Strobe,
  input  OE,
  input  in_3,
  input  in_4,
  input  in_5,
  input  in_6,
  input  in_7,
  input  in_8,
  input  in_9,
  input  in_10
);

  wire cd4094b_1_q1, cd4094b_1_q2, cd4094b_1_q3, cd4094b_1_q4, cd4094b_1_q5, cd4094b_1_q6, cd4094b_1_q7,
       cd4094b_1_q8, cd4094b_1_qs, cd4094b_1_qsinv, clock_1_out, undriven;

  Clock clock_1 (.out(clock_1_out));
  LED led_1 (.in(undriven));
  CD4094B cd4094b_1 (
    .STROBE(Strobe), .OutputEnable(OE), .DATAIN(undriven), .CLOCK(clock_1_out), .Q1(cd4094b_1_q1),
    .Q2(cd4094b_1_q2), .Q3(cd4094b_1_q3), .Q4(cd4094b_1_q4), .Q5(cd4094b_1_q5), .Q6(cd4094b_1_q6),
    .Q7(cd4094b_1_q7), .Q8(cd4094b_1_q8), .QS(cd4094b_1_qs), .QSinv(cd4094b_1_qsinv));
  LED led_2 (.in(cd4094b_1_q1));
  LED led_3 (.in(cd4094b_1_q2));
  LED led_4 (.in(cd4094b_1_q3));
  LED led_5 (.in(cd4094b_1_q4));
  LED led_6 (.in(cd4094b_1_q5));
  LED led_7 (.in(cd4094b_1_q6));
  LED led_8 (.in(cd4094b_1_q7));
  LED led_9 (.in(cd4094b_1_q8));
  LED led_10 (.in(cd4094b_1_qs));
  LED led_11 (.in(cd4094b_1_qsinv));
endmodule
