// Logisim project CD4094B_shiftNstore_nodep.circ as structural Verilog: 6 circuits, main circuit DflipFlop
module DflipFlop (
  input  READ,
  input  WRITE,
  input  data,
  input  clk,
  output mem
);

  wire and_1_out, d_ff_1_q;

  and and_1 (and_1_out, WRITE, clk);
  D_Flip_Flop d_ff_1 (.D(data), .clk(and_1_out), .Q(d_ff_1_q));  // open: Qn, preset, reset
  and and_2 (mem, READ, d_ff_1_q);
endmodule

module Latch_w_strobe (
  input  data,
  input  strobe,
  output Q,
  output Qinv
);

  wire RST, transmission_1_p3, TRinv;

  // Transmission_Gate transmission_1: pin names not known; wires that end beside it: strobe, data, transmission_1_p3, TRinv, Qinv
  S_R_Flip_Flop #(.trigger("high")) s_r_ff_1 (
    .S(transmission_1_p3), .R(RST), .clk(strobe), .Q(Q), .Qn(Qinv));  // open: reset, preset
  LED led_1 (.in(transmission_1_p3));
  not not_1 (TRinv, strobe);
  not not_2 (RST, transmission_1_p3);
  LED led_2 (.in(Q));
  LED led_3 (.in(Qinv));
  LED led_4 (.in(RST));

  // Other names for the same wires on the sheet: TR = strobe
endmodule

module CD4094B (
  input  STROBE,
  input  OutputEnable,
  input  DATAIN,
  input  CLOCK,
  output Q1,
  output Q2,
  output Q3,
  output Q4,
  output Q5,
  output Q6,
  output Q7,
  output Q8,
  output QS,
  output QSinv
);

  wire dflipflop_1_mem, dflipflop_2_mem, dflipflop_3_mem, dflipflop_4_mem, dflipflop_5_mem, dflipflop_6_mem,
       dflipflop_7_mem, dflipflop_8_mem, latch_w_strobe_1_q, latch_w_strobe_2_q, latch_w_strobe_3_q,
       latch_w_strobe_4_q, latch_w_strobe_5_q, latch_w_strobe_6_q, latch_w_strobe_7_q;

  DflipFlop dflipflop_1 (.READ(1'b1), .WRITE(1'b1), .data(DATAIN), .clk(CLOCK), .mem(dflipflop_1_mem));
  DflipFlop dflipflop_2 (.READ(1'b1), .WRITE(1'b1), .data(dflipflop_8_mem), .clk(CLOCK), .mem(dflipflop_2_mem));
  DflipFlop dflipflop_3 (.READ(1'b1), .WRITE(1'b1), .data(dflipflop_5_mem), .clk(CLOCK), .mem(dflipflop_3_mem));
  DflipFlop dflipflop_4 (.READ(1'b1), .WRITE(1'b1), .data(dflipflop_6_mem), .clk(CLOCK), .mem(dflipflop_4_mem));
  DflipFlop dflipflop_5 (.READ(1'b1), .WRITE(1'b1), .data(dflipflop_2_mem), .clk(CLOCK), .mem(dflipflop_5_mem));
  DflipFlop dflipflop_6 (.READ(1'b1), .WRITE(1'b1), .data(dflipflop_3_mem), .clk(CLOCK), .mem(dflipflop_6_mem));
  DflipFlop dflipflop_7 (.READ(1'b1), .WRITE(1'b1), .data(dflipflop_4_mem), .clk(CLOCK), .mem(dflipflop_7_mem));
  DflipFlop dflipflop_8 (.READ(1'b1), .WRITE(1'b1), .data(dflipflop_1_mem), .clk(CLOCK), .mem(dflipflop_8_mem));
  Latch_w_strobe latch_w_strobe_1 (.data(dflipflop_1_mem), .strobe(STROBE), .Q(latch_w_strobe_1_q));  // open: Qinv
  Latch_w_strobe latch_w_strobe_2 (.data(dflipflop_8_mem), .strobe(STROBE), .Q(latch_w_strobe_2_q));  // open: Qinv
  Latch_w_strobe latch_w_strobe_3 (.data(dflipflop_2_mem), .strobe(STROBE), .Q(latch_w_strobe_3_q));  // open: Qinv
  Latch_w_strobe latch_w_strobe_4 (.data(dflipflop_5_mem), .strobe(STROBE), .Q(latch_w_strobe_4_q));  // open: Qinv
  Latch_w_strobe latch_w_strobe_5 (.data(dflipflop_3_mem), .strobe(STROBE), .Q(latch_w_strobe_5_q));  // open: Qinv
  Latch_w_strobe latch_w_strobe_6 (.data(dflipflop_6_mem), .strobe(STROBE), .Q(latch_w_strobe_6_q));  // open: Qinv
  Latch_w_strobe latch_w_strobe_7 (.data(dflipflop_4_mem), .strobe(STROBE), .Q(latch_w_strobe_7_q));  // open: Qinv
  Latch_w_strobe latch_w_strobe_8 (.data(dflipflop_7_mem), .strobe(STROBE), .Q(QS));  // open: Qinv
  assign Q1 = OutputEnable ? latch_w_strobe_1_q : 1'bz;  // Controlled_Buffer controlled_buffer_1
  assign Q2 = OutputEnable ? latch_w_strobe_2_q : 1'bz;  // Controlled_Buffer controlled_buffer_2
  assign Q3 = OutputEnable ? latch_w_strobe_3_q : 1'bz;  // Controlled_Buffer controlled_buffer_3
  assign Q4 = OutputEnable ? latch_w_strobe_4_q : 1'bz;  // Controlled_Buffer controlled_buffer_4
  assign Q5 = OutputEnable ? latch_w_strobe_5_q : 1'bz;  // Controlled_Buffer controlled_buffer_5
  assign Q6 = OutputEnable ? latch_w_strobe_6_q : 1'bz;  // Controlled_Buffer controlled_buffer_6
  assign Q7 = OutputEnable ? latch_w_strobe_7_q : 1'bz;  // Controlled_Buffer controlled_buffer_7
  assign Q8 = OutputEnable ? QS : 1'bz;  // Controlled_Buffer controlled_buffer_8
  not not_1 (QSinv, QS);

  // Other names for the same wires on the sheet: CLK = CLOCK; OE = OutputEnable; STB = STROBE
endmodule

module upcntr (
  input  Reset,
  input  CLK,
  output O1,
  output O2,
  output O3,
  output O4,
  output O5,
  output O6,
  output O7,
  output O8
);

  wire and_3_out, d_ff_1_q, d_ff_2_q, d_ff_2_qn, d_ff_3_q, d_ff_3_qn, d_ff_4_q, d_ff_4_qn, d_ff_5_q,
       d_ff_5_qn, d_ff_6_q, d_ff_6_qn, d_ff_7_q, d_ff_7_qn, d_ff_8_qn, d_ff_9_q, d_ff_9_qn, not_1_out,
       not_2_out, not_3_out, not_4_out, not_5_out, not_6_out, not_7_out, or_1_out, or_2_out, or_3_out;

  or or_1 (or_1_out, Reset, and_3_out);
  D_Flip_Flop d_ff_1 (.D(1'b1), .clk(CLK), .Q(d_ff_1_q), .preset(or_1_out), .reset(or_2_out));  // open: Qn
  or or_2 (or_2_out, Reset, d_ff_9_q);
  and and_1 (O1, or_3_out, not_1_out);
  or or_3 (or_3_out, or_1_out, d_ff_1_q);
  LED led_1 (.in(O1));
  not not_1 (not_1_out, d_ff_2_q);
  D_Flip_Flop d_ff_2 (.D(d_ff_1_q), .clk(CLK), .Q(d_ff_2_q), .Qn(d_ff_2_qn), .reset(or_2_out));  // open: preset
  LED led_2 (.in(O2));
  and and_2 (O2, not_2_out, d_ff_2_q);
  D_Flip_Flop d_ff_3 (.D(d_ff_2_q), .clk(CLK), .Q(d_ff_3_q), .Qn(d_ff_3_qn), .reset(or_2_out));  // open: preset
  and and_3 (and_3_out, d_ff_2_qn, d_ff_3_qn, d_ff_4_qn, d_ff_5_qn, d_ff_6_qn, d_ff_7_qn, d_ff_8_qn, d_ff_9_qn);
  LED led_3 (.in(and_3_out));
  not not_2 (not_2_out, d_ff_3_q);
  LED led_4 (.in(O3));
  not not_3 (not_3_out, d_ff_4_q);
  and and_4 (O3, not_3_out, d_ff_3_q);
  D_Flip_Flop d_ff_4 (.D(d_ff_3_q), .clk(CLK), .Q(d_ff_4_q), .Qn(d_ff_4_qn), .reset(or_2_out));  // open: preset
  and and_5 (O4, not_4_out, d_ff_4_q);
  LED led_5 (.in(O4));
  not not_4 (not_4_out, d_ff_5_q);
  D_Flip_Flop d_ff_5 (.D(d_ff_4_q), .clk(CLK), .Q(d_ff_5_q), .Qn(d_ff_5_qn), .reset(or_2_out));  // open: preset
  and and_6 (O5, not_5_out, d_ff_5_q);
  LED led_6 (.in(O5));
  not not_5 (not_5_out, d_ff_6_q);
  D_Flip_Flop d_ff_6 (.D(d_ff_5_q), .clk(CLK), .Q(d_ff_6_q), .Qn(d_ff_6_qn), .reset(or_2_out));  // open: preset
  LED led_7 (.in(O6));
  and and_7 (O6, not_6_out, d_ff_6_q);
  not not_6 (not_6_out, d_ff_7_q);
  D_Flip_Flop d_ff_7 (.D(d_ff_6_q), .clk(CLK), .Q(d_ff_7_q), .Qn(d_ff_7_qn), .reset(or_2_out));  // open: preset
  and and_8 (O7, not_7_out, d_ff_7_q);
  LED led_8 (.in(O7));
  not not_7 (not_7_out, O8);
  D_Flip_Flop d_ff_8 (.D(d_ff_7_q), .clk(CLK), .Q(O8), .Qn(d_ff_8_qn), .reset(or_2_out));  // open: preset
  LED led_9 (.in(O8));
  D_Flip_Flop d_ff_9 (.D(O8), .clk(CLK), .Q(d_ff_9_q), .Qn(d_ff_9_qn), .reset(or_2_out));  // open: preset
endmodule

module eight_bit_seq (
  input  RESET,
  input  CLK,
  input  D1,
  input  D2,
  input  D3,
  input  D4,
  input  D6,
  input  D5,
  input  D7,
  input  D8,
  output O1,
  output O2,
  output O3,
  output O4,
  output O5,
  output O6,
  output O7,
  output O8,
  output EOS,
  output SerialOut
);

  wire controlled_buffer_1_out, controlled_buffer_2_out, controlled_buffer_3_out, controlled_buffer_4_out,
       controlled_buffer_5_out, controlled_buffer_6_out, controlled_buffer_7_out, controlled_buffer_8_out,
       upcntr_1_o1, upcntr_1_o2, upcntr_1_o3, upcntr_1_o4, upcntr_1_o5, upcntr_1_o6, upcntr_1_o7;

  upcntr upcntr_1 (
    .Reset(RESET), .CLK(CLK), .O1(upcntr_1_o1), .O2(upcntr_1_o2), .O3(upcntr_1_o3), .O4(upcntr_1_o4),
    .O5(upcntr_1_o5), .O6(upcntr_1_o6), .O7(upcntr_1_o7), .O8(EOS));
  assign controlled_buffer_1_out = upcntr_1_o1 ? D1 : 1'bz;  // Controlled_Buffer controlled_buffer_1
  and and_1 (O1, upcntr_1_o1, controlled_buffer_1_out);
  assign controlled_buffer_2_out = upcntr_1_o5 ? D5 : 1'bz;  // Controlled_Buffer controlled_buffer_2
  and and_2 (O2, upcntr_1_o2, controlled_buffer_3_out);
  assign controlled_buffer_3_out = upcntr_1_o2 ? D2 : 1'bz;  // Controlled_Buffer controlled_buffer_3
  and and_3 (O5, upcntr_1_o5, controlled_buffer_2_out);
  and and_4 (O6, upcntr_1_o6, controlled_buffer_4_out);
  assign controlled_buffer_4_out = upcntr_1_o6 ? D6 : 1'bz;  // Controlled_Buffer controlled_buffer_4
  and and_5 (O3, upcntr_1_o3, controlled_buffer_5_out);
  assign controlled_buffer_5_out = upcntr_1_o3 ? D3 : 1'bz;  // Controlled_Buffer controlled_buffer_5
  and and_6 (O7, upcntr_1_o7, controlled_buffer_6_out);
  assign controlled_buffer_6_out = upcntr_1_o7 ? D7 : 1'bz;  // Controlled_Buffer controlled_buffer_6
  and and_7 (O4, upcntr_1_o4, controlled_buffer_7_out);
  assign controlled_buffer_7_out = upcntr_1_o4 ? D4 : 1'bz;  // Controlled_Buffer controlled_buffer_7
  and and_8 (O8, EOS, controlled_buffer_8_out);
  assign controlled_buffer_8_out = EOS ? D8 : 1'bz;  // Controlled_Buffer controlled_buffer_8
  LED led_1 (.in(SerialOut));
  LED led_2 (.in(CLK));
  or or_1 (SerialOut, O1, O2, O3, O4, O5, O6, O7, O8);
endmodule

module CD4094TEST (
  input  Strobe,
  input  OE,
  input  in_3,
  input  in_4,
  input  in_5,
  input  in_6,
  input  in_7,
  input  in_8,
  input  in_9,
  input  in_10
);

  wire cd4094b_1_q1, cd4094b_1_q2, cd4094b_1_q3, cd4094b_1_q4, cd4094b_1_q5, cd4094b_1_q6, cd4094b_1_q7,
       cd4094b_1_q8, cd4094b_1_qs, cd4094b_1_qsinv, clock_1_out, eight_bit_seq_1_serialout;

  Clock clock_1 (.out(clock_1_out));
  eight_bit_seq eight_bit_seq_1 (
    .CLK(clock_1_out), .D1(in_3), .D2(in_4), .D3(in_5), .D4(in_6), .D6(in_7), .D5(in_8), .D7(in_9),
    .D8(in_10), .SerialOut(eight_bit_seq_1_serialout));  // open: RESET, O1, O2, O3, O4, O5, O6, O7, O8, EOS
  LED led_1 (.in(eight_bit_seq_1_serialout));
  CD4094B cd4094b_1 (
    .STROBE(Strobe), .OutputEnable(OE), .DATAIN(eight_bit_seq_1_serialout), .CLOCK(clock_1_out),
    .Q1(cd4094b_1_q1), .Q2(cd4094b_1_q2), .Q3(cd4094b_1_q3), .Q4(cd4094b_1_q4), .Q5(cd4094b_1_q5),
    .Q6(cd4094b_1_q6), .Q7(cd4094b_1_q7), .Q8(cd4094b_1_q8), .QS(cd4094b_1_qs), .QSinv(cd4094b_1_qsinv));
  LED led_2 (.in(cd4094b_1_q1));
  LED led_3 (.in(cd4094b_1_q2));
  LED led_4 (.in(cd4094b_1_q3));
  LED led_5 (.in(cd4094b_1_q4));
  LED led_6 (.in(cd4094b_1_q5));
  LED led_7 (.in(cd4094b_1_q6));
  LED led_8 (.in(cd4094b_1_q7));
  LED led_9 (.in(cd4094b_1_q8));
  LED led_10 (.in(cd4094b_1_qs));
  LED led_11 (.in(cd4094b_1_qsinv));
endmodule
