// Logisim project EightbitSequencer.circ as structural Verilog: 1 circuit, main circuit EightBitSeq
module EightBitSeq (
  input  RESET,
  input  CLK,
  input  D1,
  input  D2,
  input  D3,
  input  D4,
  input  D6,
  input  D5,
  input  D7,
  input  D8,
  output O1,
  output O2,
  output O3,
  output O4,
  output O5,
  output O6,
  output O7,
  output O8,
  output EOS,
  output SerialOut
);

  wire controlled_buffer_1_out, controlled_buffer_2_out, controlled_buffer_3_out, controlled_buffer_4_out,
       controlled_buffer_5_out, controlled_buffer_6_out, controlled_buffer_7_out, controlled_buffer_8_out,
       upcounter_1_p3, upcounter_1_p4, upcounter_1_p5, upcounter_1_p6, upcounter_1_p7, upcounter_1_p8,
       upcounter_1_p9;

  // upcounter upcounter_1: pin names not known; wires that end beside it: RESET, CLK, upcounter_1_p3, upcounter_1_p4, upcounter_1_p5, upcounter_1_p6, upcounter_1_p7, upcounter_1_p8, upcounter_1_p9, EOS
  assign controlled_buffer_1_out = upcounter_1_p3 ? D1 : 1'bz;  // Controlled_Buffer controlled_buffer_1
  and and_1 (O1, upcounter_1_p3, controlled_buffer_1_out);
  assign controlled_buffer_2_out = upcounter_1_p7 ? D5 : 1'bz;  // Controlled_Buffer controlled_buffer_2
  and and_2 (O2, upcounter_1_p4, controlled_buffer_3_out);
  assign controlled_buffer_3_out = upcounter_1_p4 ? D2 : 1'bz;  // Controlled_Buffer controlled_buffer_3
  and and_3 (O5, upcounter_1_p7, controlled_buffer_2_out);
  and and_4 (O6, upcounter_1_p8, controlled_buffer_4_out);
  assign controlled_buffer_4_out = upcounter_1_p8 ? D6 : 1'bz;  // Controlled_Buffer controlled_buffer_4
  and and_5 (O3, upcounter_1_p5, controlled_buffer_5_out);
  assign controlled_buffer_5_out = upcounter_1_p5 ? D3 : 1'bz;  // Controlled_Buffer controlled_buffer_5
  and and_6 (O7, upcounter_1_p9, controlled_buffer_6_out);
  assign controlled_buffer_6_out = upcounter_1_p9 ? D7 : 1'bz;  // Controlled_Buffer controlled_buffer_6
  and and_7 (O4, upcounter_1_p6, controlled_buffer_7_out);
  assign controlled_buffer_7_out = upcounter_1_p6 ? D4 : 1'bz;  // Controlled_Buffer controlled_buffer_7
  and and_8 (O8, EOS, controlled_buffer_8_out);
  assign controlled_buffer_8_out = EOS ? D8 : 1'bz;  // Controlled_Buffer controlled_buffer_8
  LED led_1 (.in(SerialOut));
  LED led_2 (.in(CLK));
  or or_1 (SerialOut, O1, O2, O3, O4, O5, O6, O7, O8);
endmodule
