// Logisim project EightbitSequencer_nodep.circ as structural Verilog: 2 circuits, main circuit EightBitSeq
module upcount (
  input  Reset,
  input  CLK,
  output O1,
  output O2,
  output O3,
  output O4,
  output O5,
  output O6,
  output O7,
  output O8
);

  wire and_3_out, d_ff_1_q, d_ff_2_q, d_ff_2_qn, d_ff_3_q, d_ff_3_qn, d_ff_4_q, d_ff_4_qn, d_ff_5_q,
       d_ff_5_qn, d_ff_6_q, d_ff_6_qn, d_ff_7_q, d_ff_7_qn, d_ff_8_qn, d_ff_9_q, d_ff_9_qn, not_1_out,
       not_2_out, not_3_out, not_4_out, not_5_out, not_6_out, not_7_out, or_1_out, or_2_out, or_3_out;

  or or_1 (or_1_out, Reset, and_3_out);
  D_Flip_Flop d_ff_1 (.D(1'b1), .clk(CLK), .Q(d_ff_1_q), .preset(or_1_out), .reset(or_2_out));  // open: Qn
  or or_2 (or_2_out, Reset, d_ff_9_q);
  and and_1 (O1, or_3_out, not_1_out);
  or or_3 (or_3_out, or_1_out, d_ff_1_q);
  LED led_1 (.in(O1));
  not not_1 (not_1_out, d_ff_2_q);
  D_Flip_Flop d_ff_2 (.D(d_ff_1_q), .clk(CLK), .Q(d_ff_2_q), .Qn(d_ff_2_qn), .reset(or_2_out));  // open: preset
  LED led_2 (.in(O2));
  and and_2 (O2, not_2_out, d_ff_2_q);
  D_Flip_Flop d_ff_3 (.D(d_ff_2_q), .clk(CLK), .Q(d_ff_3_q), .Qn(d_ff_3_qn), .reset(or_2_out));  // open: preset
  and and_3 (and_3_out, d_ff_2_qn, d_ff_3_qn, d_ff_4_qn, d_ff_5_qn, d_ff_6_qn, d_ff_7_qn, d_ff_8_qn, d_ff_9_qn);
  LED led_3 (.in(and_3_out));
  not not_2 (not_2_out, d_ff_3_q);
  LED led_4 (.in(O3));
  not not_3 (not_3_out, d_ff_4_q);
  and and_4 (O3, not_3_out, d_ff_3_q);
  D_Flip_Flop d_ff_4 (.D(d_ff_3_q), .clk(CLK), .Q(d_ff_4_q), .Qn(d_ff_4_qn), .reset(or_2_out));  // open: preset
  and and_5 (O4, not_4_out, d_ff_4_q);
  LED led_5 (.in(O4));
  not not_4 (not_4_out, d_ff_5_q);
  D_Flip_Flop d_ff_5 (.D(d_ff_4_q), .clk(CLK), .Q(d_ff_5_q), .Qn(d_ff_5_qn), .reset(or_2_out));  // open: preset
  and and_6 (O5, not_5_out, d_ff_5_q);
  LED led_6 (.in(O5));
  not not_5 (not_5_out, d_ff_6_q);
  D_Flip_Flop d_ff_6 (.D(d_ff_5_q), .clk(CLK), .Q(d_ff_6_q), .Qn(d_ff_6_qn), .reset(or_2_out));  // open: preset
  LED led_7 (.in(O6));
  and and_7 (O6, not_6_out, d_ff_6_q);
  not not_6 (not_6_out, d_ff_7_q);
  D_Flip_Flop d_ff_7 (.D(d_ff_6_q), .clk(CLK), .Q(d_ff_7_q), .Qn(d_ff_7_qn), .reset(or_2_out));  // open: preset
  and and_8 (O7, not_7_out, d_ff_7_q);
  LED led_8 (.in(O7));
  not not_7 (not_7_out, O8);
  D_Flip_Flop d_ff_8 (.D(d_ff_7_q), .clk(CLK), .Q(O8), .Qn(d_ff_8_qn), .reset(or_2_out));  // open: preset
  LED led_9 (.in(O8));
  D_Flip_Flop d_ff_9 (.D(O8), .clk(CLK), .Q(d_ff_9_q), .Qn(d_ff_9_qn), .reset(or_2_out));  // open: preset
endmodule

module EightBitSeq (
  input  RESET,
  input  CLK,
  input  D1,
  input  D2,
  input  D3,
  input  D4,
  input  D6,
  input  D5,
  input  D7,
  input  D8,
  output O1,
  output O2,
  output O3,
  output O4,
  output O5,
  output O6,
  output O7,
  output O8,
  output EOS,
  output SerialOut
);

  wire controlled_buffer_1_out, controlled_buffer_2_out, controlled_buffer_3_out, controlled_buffer_4_out,
       controlled_buffer_5_out, controlled_buffer_6_out, controlled_buffer_7_out, controlled_buffer_8_out,
       upcount_1_o1, upcount_1_o2, upcount_1_o3, upcount_1_o4, upcount_1_o5, upcount_1_o6, upcount_1_o7;

  upcount upcount_1 (
    .Reset(RESET), .CLK(CLK), .O1(upcount_1_o1), .O2(upcount_1_o2), .O3(upcount_1_o3), .O4(upcount_1_o4),
    .O5(upcount_1_o5), .O6(upcount_1_o6), .O7(upcount_1_o7), .O8(EOS));
  assign controlled_buffer_1_out = upcount_1_o1 ? D1 : 1'bz;  // Controlled_Buffer controlled_buffer_1
  and and_1 (O1, upcount_1_o1, controlled_buffer_1_out);
  assign controlled_buffer_2_out = upcount_1_o5 ? D5 : 1'bz;  // Controlled_Buffer controlled_buffer_2
  and and_2 (O2, upcount_1_o2, controlled_buffer_3_out);
  assign controlled_buffer_3_out = upcount_1_o2 ? D2 : 1'bz;  // Controlled_Buffer controlled_buffer_3
  and and_3 (O5, upcount_1_o5, controlled_buffer_2_out);
  and and_4 (O6, upcount_1_o6, controlled_buffer_4_out);
  assign controlled_buffer_4_out = upcount_1_o6 ? D6 : 1'bz;  // Controlled_Buffer controlled_buffer_4
  and and_5 (O3, upcount_1_o3, controlled_buffer_5_out);
  assign controlled_buffer_5_out = upcount_1_o3 ? D3 : 1'bz;  // Controlled_Buffer controlled_buffer_5
  and and_6 (O7, upcount_1_o7, controlled_buffer_6_out);
  assign controlled_buffer_6_out = upcount_1_o7 ? D7 : 1'bz;  // Controlled_Buffer controlled_buffer_6
  and and_7 (O4, upcount_1_o4, controlled_buffer_7_out);
  assign controlled_buffer_7_out = upcount_1_o4 ? D4 : 1'bz;  // Controlled_Buffer controlled_buffer_7
  and and_8 (O8, EOS, controlled_buffer_8_out);
  assign controlled_buffer_8_out = EOS ? D8 : 1'bz;  // Controlled_Buffer controlled_buffer_8
  LED led_1 (.in(SerialOut));
  LED led_2 (.in(CLK));
  or or_1 (SerialOut, O1, O2, O3, O4, O5, O6, O7, O8);
endmodule
