// Logisim project HEF4018_divide_by_n.circ as structural Verilog: 3 circuits, main circuit HEF4018B
module HEF4018B (
  input  P0,
  input  P1,
  input  P2,
  input  P3,
  input  P4,
  input  D,
  input  CLK,
  input  PL,
  input  MR,
  output O0INV,
  output O1INV,
  output O2INV,
  output O3INV,
  output O4INV
);

  wire and_1_out, and_2_out, and_3_out, and_4_out, and_5_out, and_6_out, and_8_out, and_9_out, and_10_out,
       and_11_out, d_ff_1_q, d_ff_2_q, d_ff_3_q, d_ff_4_q, d_ff_5_q, F3, MR_t, MRINV, not_3_out, not_4_out,
       not_6_out, not_7_out, not_9_out, not_10_out, not_12_out, not_13_out, not_15_out, not_16_out, or_1_out,
       or_2_out, or_3_out, or_4_out, or_5_out, or_6_out;

  not not_1 (MR_t, MR);
  not not_2 (MRINV, MR_t);
  not not_3 (not_3_out, P0);
  not not_4 (not_4_out, not_3_out);
  and and_1 (and_1_out, MR_t, PL, not_4_out);
  D_Flip_Flop d_ff_1 (.D(D), .clk(CLK), .Q(d_ff_1_q), .preset(and_1_out), .reset(or_1_out));  // open: Qn
  or or_1 (or_1_out, MRINV, and_2_out);
  and and_2 (and_2_out, MR_t, PL, not_3_out);
  not not_5 (O0INV, d_ff_1_q);
  LED led_1 (.in(O0INV));
  and and_3 (and_3_out, MR_t, PL, not_7_out);
  D_Flip_Flop d_ff_2 (.D(d_ff_1_q), .clk(CLK), .Q(d_ff_2_q), .preset(and_3_out), .reset(or_2_out));  // open: Qn
  or or_2 (or_2_out, MRINV, and_4_out);
  and and_4 (and_4_out, MR_t, PL, not_6_out);
  or or_3 (or_3_out, d_ff_3_q, d_ff_1_q);
  not not_6 (not_6_out, P1);
  not not_7 (not_7_out, not_6_out);
  not not_8 (O1INV, d_ff_2_q);
  LED led_2 (.in(O1INV));
  and and_5 (and_5_out, MR_t, PL, not_10_out);
  D_Flip_Flop d_ff_3 (.D(F3), .clk(CLK), .Q(d_ff_3_q), .reset(or_4_out));  // open: Qn, preset
  or or_4 (or_4_out, MRINV, and_6_out);
  not not_9 (not_9_out, P2);
  not not_10 (not_10_out, not_9_out);
  and and_6 (and_6_out, MR_t, PL, not_9_out);
  and and_7 (F3, d_ff_2_q, or_3_out);
  not not_11 (O2INV, d_ff_3_q);
  LED led_3 (.in(O2INV));
  D_Flip_Flop d_ff_4 (.D(d_ff_3_q), .clk(CLK), .Q(d_ff_4_q), .preset(and_8_out), .reset(or_5_out));  // open: Qn
  not not_12 (not_12_out, P3);
  not not_13 (not_13_out, not_12_out);
  and and_8 (and_8_out, MR_t, PL, not_13_out);
  or or_5 (or_5_out, MRINV, and_9_out);
  and and_9 (and_9_out, MR_t, PL, not_12_out);
  not not_14 (O3INV, d_ff_4_q);
  D_Flip_Flop d_ff_5 (.D(d_ff_4_q), .clk(CLK), .Q(d_ff_5_q), .preset(and_10_out), .reset(or_6_out));  // open: Qn
  LED led_4 (.in(O3INV));
  not not_15 (not_15_out, P4);
  not not_16 (not_16_out, not_15_out);
  and and_10 (and_10_out, MR_t, PL, not_16_out);
  or or_6 (or_6_out, MRINV, and_11_out);
  and and_11 (and_11_out, MR_t, PL, not_15_out);
  not not_17 (O4INV, d_ff_5_q);
  LED led_5 (.in(O4INV));
endmodule

module HEF4018TEST (
);

  wire clock_1_out, d_ff_1_q, d_ff_1_qn, hef4018b_1_o1inv, hef4018b_2_o0inv, hef4018b_2_o2inv,
       hef4018b_2_o3inv, hef4018b_3_o0inv, hef4018b_3_o1inv, hef4018b_3_o2inv, hef4018b_3_o3inv,
       hef4018b_3_o4inv, hef4018b_4_o0inv, hef4018b_4_o1inv, hef4018b_4_o2inv, hef4018b_4_o3inv,
       hef4018b_5_o0inv, hef4018b_5_o1inv, hef4018b_5_o2inv, hef4018b_5_o3inv, nand_1_out, nand_2_out,
       nand_3_out, nand_4_out, not_1_out, not_2_out, not_3_out, not_4_out;

  Clock clock_1 (.out(clock_1_out));
  not not_1 (not_1_out, nand_1_out);
  not not_2 (not_2_out, nand_2_out);
  HEF4018B hef4018b_1 (
    .D(hef4018b_1_o1inv), .CLK(clock_1_out), .PL(1'b0), .MR(1'b0), .O1INV(hef4018b_1_o1inv));  // open: P0, P1, P2, P3, P4, O0INV, O2INV, O3INV, O4INV
  HEF4018B hef4018b_2 (
    .D(not_1_out), .CLK(clock_1_out), .PL(1'b0), .MR(1'b0), .O0INV(hef4018b_2_o0inv),
    .O2INV(hef4018b_2_o2inv), .O3INV(hef4018b_2_o3inv));  // open: P0, P1, P2, P3, P4, O1INV, O4INV
  HEF4018B hef4018b_3 (
    .D(not_2_out), .CLK(clock_1_out), .PL(1'b0), .MR(1'b0), .O0INV(hef4018b_3_o0inv),
    .O1INV(hef4018b_3_o1inv), .O2INV(hef4018b_3_o2inv), .O3INV(hef4018b_3_o3inv), .O4INV(hef4018b_3_o4inv));  // open: P0, P1, P2, P3, P4
  // Digital_Oscilloscope digital_oscilloscope_1: pin names not known; wires that end beside it: hef4018b_1_o1inv, clock_1_out, hef4018b_1_o1inv
  nand nand_1 (nand_1_out, hef4018b_2_o2inv, hef4018b_2_o3inv);
  nand nand_2 (nand_2_out, hef4018b_3_o3inv, hef4018b_3_o4inv);
  // Digital_Oscilloscope digital_oscilloscope_2: pin names not known; wires that end beside it: hef4018b_2_o0inv, hef4018b_2_o2inv, hef4018b_2_o3inv, clock_1_out, hef4018b_2_o0inv
  // Digital_Oscilloscope digital_oscilloscope_3: pin names not known; wires that end beside it: hef4018b_3_o0inv, hef4018b_3_o2inv, hef4018b_3_o3inv, clock_1_out, hef4018b_3_o1inv
  D_Flip_Flop d_ff_1 (.D(d_ff_1_qn), .clk(hef4018b_1_o1inv), .Q(d_ff_1_q), .Qn(d_ff_1_qn));  // open: preset, reset
  // Digital_Oscilloscope digital_oscilloscope_4: pin names not known; wires that end beside it: d_ff_1_q, clock_1_out, clock_1_out, d_ff_1_q
  not not_3 (not_3_out, nand_4_out);
  not not_4 (not_4_out, nand_3_out);
  HEF4018B hef4018b_4 (
    .D(not_3_out), .CLK(clock_1_out), .PL(1'b0), .MR(1'b0), .O0INV(hef4018b_4_o0inv),
    .O1INV(hef4018b_4_o1inv), .O2INV(hef4018b_4_o2inv), .O3INV(hef4018b_4_o3inv));  // open: P0, P1, P2, P3, P4, O4INV
  HEF4018B hef4018b_5 (
    .D(not_4_out), .CLK(clock_1_out), .PL(1'b0), .MR(1'b0), .O0INV(hef4018b_5_o0inv),
    .O1INV(hef4018b_5_o1inv), .O2INV(hef4018b_5_o2inv), .O3INV(hef4018b_5_o3inv));  // open: P0, P1, P2, P3, P4, O4INV
  nand nand_3 (nand_3_out, hef4018b_5_o1inv, hef4018b_5_o2inv);
  nand nand_4 (nand_4_out, hef4018b_4_o0inv, hef4018b_4_o1inv);
  // Digital_Oscilloscope digital_oscilloscope_5: pin names not known; wires that end beside it: hef4018b_4_o0inv, hef4018b_4_o2inv, hef4018b_4_o3inv, clock_1_out, hef4018b_4_o0inv
  // Digital_Oscilloscope digital_oscilloscope_6: pin names not known; wires that end beside it: hef4018b_5_o0inv, hef4018b_5_o2inv, hef4018b_5_o3inv, hef4018b_5_o2inv, clock_1_out, hef4018b_5_o0inv

  // Notes on the sheet:
  //   Even divisors, move the loop between O0Inv, O1inv, 02inv etc and D to see different results
  //   O to Data 4 output is 5 rise, 5 fall
  //   This config is 9 rise, 7 fall
  //   This config is 11 rise, 9 fall
  //   O to Data 0 output is 1 rise, 1 fall
  //   O to Data 1 output is 2 rise, 2 fall
  //   O to Data 2 output is 3 rise, 3 fall
  //   O to Data 3 output is 4 rise, 4 fall
  //   T flip flop divides by 2 giving expected results
  //   This config is 5 rise, 3 fall
  //   This config is 7 rise, 5 fall
endmodule

module HEF4018SONOFTEST (
  input  in_1
);

  wire and_1_out, and_2_out, clock_1_out, comparator_1_gt, d_ff_1_q, d_ff_1_qn, digital_oscilloscope_1_p2,
       hef4018b_1_o0inv;
  wire [7:0] counter_1_q;

  Clock clock_1 (.out(clock_1_out));
  Counter #(.max('h10)) counter_1 (
    .clr(in_1), .count(1'b1), .clk(clock_1_out), .Q(counter_1_q));  // open: load, up, D, carry
  Comparator comparator_1 (.a(8'h7), .b(counter_1_q), .gt(comparator_1_gt));  // open: eq, lt
  and and_1 (and_1_out, clock_1_out, comparator_1_gt);
  D_Flip_Flop d_ff_1 (
    .D(d_ff_1_qn), .clk(digital_oscilloscope_1_p2), .Q(d_ff_1_q), .Qn(d_ff_1_qn));  // open: preset, reset
  // Digital_Oscilloscope digital_oscilloscope_1: pin names not known; wires that end beside it: clock_1_out, digital_oscilloscope_1_p2
  // Digital_Oscilloscope digital_oscilloscope_2: pin names not known; wires that end beside it: clock_1_out, d_ff_1_q
  HEF4018B hef4018b_1 (
    .D(and_2_out), .CLK(and_1_out), .PL(1'b0), .MR(1'b0), .O0INV(hef4018b_1_o0inv),
    .O1INV(digital_oscilloscope_1_p2));  // open: P0, P1, P2, P3, P4, O2INV, O3INV, O4INV
  and and_2 (and_2_out, hef4018b_1_o0inv, digital_oscilloscope_1_p2);

  // Notes on the sheet:
  //   10 divided by 3
  //   Again by using a T flop we can see a count of 10 leaves 3 remaining.
endmodule
