// Logisim project MC14585B_4_bit_magnitude_comparator.circ as structural Verilog: 1 circuit, main circuit MC14585B
module MC14585B (
  input  A3,
  input  B3,
  input  A2,
  input  B2,
  input  A1,
  input  B1,
  input  A0,
  input  B0,
  input  AeqB,
  input  A_lt_B,
  input  A_gt_B,
  output AgtrB,
  output A_EQ_B,
  output AlessthanB
);

  wire nand_1_out, nand_2_out, nand_3_out, nand_4_out, nand_5_out, nand_6_out, nand_7_out, nand_8_out,
       nand_12_out, nand_13_out, nor_1_out, nor_2_out, not_1_out, not_2_out, not_3_out, not_4_out, not_5_out,
       not_6_out, not_7_out, not_8_out, not_9_out, not_10_out, not_11_out, not_12_out, not_13_out, or_1_out,
       or_2_out, or_3_out, or_4_out, X, Y, Z;

  not not_1 (not_1_out, A3);
  not not_2 (not_2_out, B3);
  not not_3 (not_3_out, A2);
  not not_4 (not_4_out, B2);
  not not_5 (not_5_out, A1);
  not not_6 (not_6_out, B1);
  not not_7 (not_7_out, A0);
  not not_8 (not_8_out, B0);
  nand nand_1 (nand_1_out, not_1_out, B3);
  nand nand_2 (nand_2_out, A3, not_2_out);
  nand nand_3 (nand_3_out, not_3_out, B2);
  nand nand_4 (nand_4_out, A2, not_4_out);
  nand nand_5 (nand_5_out, not_5_out, B1);
  nand nand_6 (nand_6_out, A1, not_6_out);
  nand nand_7 (nand_7_out, not_7_out, B0);
  nand nand_8 (nand_8_out, A0, not_8_out);
  nand nand_9 (X, nand_1_out, nand_2_out);
  nand nand_10 (Y, nand_3_out, nand_4_out);
  nand nand_11 (Z, nand_5_out, nand_6_out);
  nand nand_12 (nand_12_out, nand_7_out, nand_8_out);
  // NoConnect on A_gt_B
  or or_1 (or_1_out, X, nand_3_out);
  or or_2 (or_2_out, X, Y, nand_5_out);
  or or_3 (or_3_out, X, Y, Z, nand_7_out);
  or or_4 (or_4_out, X, Y, Z, nand_12_out, AeqB);
  nor nor_1 (nor_1_out, X, Y, Z, nand_12_out, A_lt_B);
  nand nand_13 (nand_13_out, nand_1_out, or_1_out, or_2_out, or_3_out, or_4_out);
  not not_9 (not_9_out, nand_13_out);
  not not_10 (not_10_out, nor_1_out);
  nor nor_2 (nor_2_out, nand_13_out, nor_1_out);
  not not_11 (not_11_out, nor_2_out);
  and and_1 (AgtrB, not_9_out, not_10_out);
  and and_2 (AlessthanB, not_10_out, not_11_out);
  not not_12 (not_12_out, AgtrB);
  not not_13 (not_13_out, AlessthanB);
  and and_3 (A_EQ_B, not_12_out, not_13_out);
endmodule
