// Logisim project RotaryEncoder2a.circ as structural Verilog: 1 circuit, main circuit rotaryEncoder
module rotaryEncoder (
  input  Data,
  input  RUN,
  input  CONTINUE,
  input  DIRECTION,
  output A,
  output B,
  output NAND_A,
  output NAND_B
);

  wire ACCW, ACW, BCCW, BCW, CLK, controlled_buffer_1_out, d_ff_3_q, d_ff_4_q, d_ff_7_q, d_ff_8_q,
       nand_1_out, nand_2_out, or_1_out, P1OFF, P1ON, P2OFF, P2ON;

  or or_1 (or_1_out, d_ff_8_q, Data);
  Clock clock_1 (.out(CLK));
  D_Flip_Flop d_ff_1 (.D(or_1_out), .clk(CLK), .Q(P1ON), .preset(RUN));  // open: Qn, reset
  T_Flip_Flop t_ff_1 (.Q(ACW), .reset(P1OFF), .preset(P1ON));  // open: T, clk, Qn
  T_Flip_Flop t_ff_2 (.Q(ACCW), .reset(P2OFF), .preset(P2ON));  // open: T, clk, Qn
  LED led_1 (.in(P1ON));
  LED led_2 (.in(ACW));
  LED led_3 (.in(ACCW));
  D_Flip_Flop d_ff_2 (.D(P1ON), .clk(CLK), .Q(P2ON), .reset(RUN));  // open: Qn, preset
  LED led_4 (.in(P2ON));
  Multiplexer multiplexer_1 (.in0(ACW), .in1(ACCW), .out(A), .sel(DIRECTION));
  Multiplexer multiplexer_2 (.in0(BCW), .in1(BCCW), .out(B), .sel(DIRECTION));
  D_Flip_Flop d_ff_3 (.D(P2ON), .clk(CLK), .Q(d_ff_3_q), .reset(RUN));  // open: Qn, preset
  T_Flip_Flop t_ff_3 (.Q(BCW), .reset(P2OFF), .preset(P2ON));  // open: T, clk, Qn
  T_Flip_Flop t_ff_4 (.Q(BCCW), .reset(P1OFF), .preset(P1ON));  // open: T, clk, Qn
  LED led_5 (.in(d_ff_3_q));
  LED led_6 (.in(BCW));
  LED led_7 (.in(BCCW));
  D_Flip_Flop d_ff_4 (.D(d_ff_3_q), .clk(CLK), .Q(d_ff_4_q), .reset(RUN));  // open: Qn, preset
  // Digital_Oscilloscope #(.frontlines("no"), .nState(12), .showclock("false")) digital_oscilloscope_1: pin names not known; wires that end beside it: CLK, ACW, BCW
  // Digital_Oscilloscope #(.frontlines("no"), .nState(12), .showclock("false")) digital_oscilloscope_2: pin names not known; wires that end beside it: CLK, ACCW, BCCW
  LED led_8 (.in(d_ff_4_q));
  nand nand_1 (nand_1_out, A, nand_2_out);
  nand nand_2 (nand_2_out, nand_1_out, B);
  LED led_9 (.in(P1OFF));
  D_Flip_Flop d_ff_5 (.D(d_ff_4_q), .clk(CLK), .Q(P1OFF), .reset(RUN));  // open: Qn, preset
  nand nand_3 (NAND_A, A, nand_1_out);
  nand nand_4 (NAND_B, nand_2_out, B);
  LED led_10 (.in(P2OFF));
  D_Flip_Flop d_ff_6 (.D(P1OFF), .clk(CLK), .Q(P2OFF), .reset(RUN));  // open: Qn, preset
  LED led_11 (.in(NAND_A));
  LED led_12 (.in(NAND_B));
  D_Flip_Flop d_ff_7 (.D(P2OFF), .clk(CLK), .Q(d_ff_7_q), .reset(RUN));  // open: Qn, preset
  LED led_13 (.in(d_ff_7_q));
  D_Flip_Flop d_ff_8 (.D(d_ff_7_q), .clk(controlled_buffer_1_out), .Q(d_ff_8_q), .reset(RUN));  // open: Qn, preset
  assign controlled_buffer_1_out = CONTINUE ? CLK : 1'bz;  // Controlled_Buffer controlled_buffer_1
  LED led_14 (.in(d_ff_8_q));

  // Other names for the same wires on the sheet: P3OFF = P2OFF; P3ON = P2ON; P4OFF = P1OFF; P4ON = P1ON

  // Notes on the sheet:
  //   RING COUNTER
  //   AB CW
  //   AB CCW
  //   A and B follow normal encoder logic.
  //   NAND A and B: A changes for CW while B does not change; B changes for CCW while A does not change
endmodule
