// Logisim project SR_used_as_toggle.circ as structural Verilog: 1 circuit, main circuit main
module main (
  input  in_1,
  input  in_2,
  input  in_3
);

  wire clock_1_out, not_1_out, s_r_ff_1_q, s_r_ff_1_qn;

  Clock clock_1 (.out(clock_1_out));
  not not_1 (not_1_out, in_2);
  S_R_Flip_Flop s_r_ff_1 (
    .S(in_2), .R(not_1_out), .clk(clock_1_out), .Q(s_r_ff_1_q), .reset(in_3), .Qn(s_r_ff_1_qn), .preset(in_1));
  LED led_1 (.in(s_r_ff_1_q));
  LED led_2 (.in(s_r_ff_1_qn));
endmodule
