// Logisim project THREE_digit_hex_counter3.circ as structural Verilog: 1 circuit, main circuit main
module main (
  input  RESET
);

  wire and_1_out, CARRY, CLK, comparator_1_eq, comparator_1_lt, comparator_2_eq, comparator_3_eq,
       comparator_4_eq, comparator_5_eq, comparator_5_lt, comparator_6_eq, d_ff_1_q, d_ff_2_q, d_ff_3_q,
       d_ff_4_q, undriven, undriven_2;
  wire [3:0] counter_1_q, counter_2_q, counter_3_q;

  Clock clock_1 (.out(CLK));
  Counter #(.max('hf), .width(4)) counter_1 (
    .clr(RESET), .load(undriven), .up(1'b1), .clk(CLK), .Q(counter_1_q));  // open: count, D, carry
  Counter #(.max('hf), .width(4)) counter_2 (
    .clr(RESET), .load(undriven_2), .up(1'b1), .clk(CARRY), .Q(counter_2_q));  // open: count, D, carry
  Counter #(.max('hf), .width(4)) counter_3 (
    .clr(RESET), .up(1'b1), .clk(and_1_out), .Q(counter_3_q));  // open: load, count, D, carry
  Hex_Digit_Display hex_digit_display_1 (.value(counter_3_q));  // open: dp
  Hex_Digit_Display hex_digit_display_2 (.value(counter_2_q));  // open: dp
  Hex_Digit_Display hex_digit_display_3 (.value(counter_1_q));  // open: dp
  Comparator #(.mode("unsigned"), .width(4)) comparator_1 (
    .a(4'b1111), .b(counter_2_q), .eq(comparator_1_eq), .lt(comparator_1_lt));  // open: gt
  Comparator #(.mode("unsigned"), .width(4)) comparator_2 (
    .a(4'b0000), .b(counter_2_q), .eq(comparator_2_eq));  // open: gt, lt
  Comparator #(.mode("unsigned"), .width(4)) comparator_3 (
    .a(4'b0001), .b(counter_2_q), .eq(comparator_3_eq));  // open: gt, lt
  D_Flip_Flop d_ff_1 (.clk(CLK), .Q(d_ff_1_q), .preset(comparator_1_eq), .reset(comparator_3_eq));  // open: D, Qn
  D_Flip_Flop d_ff_2 (.Q(d_ff_2_q), .preset(comparator_2_eq), .reset(comparator_3_eq));  // open: D, clk, Qn
  Comparator #(.mode("unsigned"), .width(4)) comparator_4 (
    .a(4'b0001), .b(counter_1_q), .eq(comparator_4_eq));  // open: gt, lt
  Comparator #(.mode("unsigned"), .width(4)) comparator_5 (
    .a(4'b1111), .b(counter_1_q), .eq(comparator_5_eq), .lt(comparator_5_lt));  // open: gt
  D_Flip_Flop d_ff_3 (.clk(CLK), .Q(d_ff_3_q), .preset(comparator_5_eq), .reset(comparator_4_eq));  // open: D, Qn
  Comparator #(.mode("unsigned"), .width(4)) comparator_6 (
    .a(4'b0000), .b(counter_1_q), .eq(comparator_6_eq));  // open: gt, lt
  and and_1 (and_1_out, d_ff_2_q, d_ff_1_q);
  D_Flip_Flop d_ff_4 (.Q(d_ff_4_q), .preset(comparator_6_eq), .reset(comparator_4_eq));  // open: D, clk, Qn
  and and_2 (CARRY, d_ff_4_q, d_ff_3_q);

  // Notes on the sheet:
  //   LOGISIM'S COUNTER CARRY IS SET TO F, NOT 1+F, 2X D MEMORY BELOW TURNS THAT INTO 1+F
endmodule
