// Logisim project johnson_ring_4nodes.circ as structural Verilog: 1 circuit, main circuit main
module main (
  input  OmyJohnson,
  input  Data,
  input  Reset
);

  wire and_1_out, and_2_out, clock_1_out, d_ff_1_q, d_ff_2_q, d_ff_3_q, d_ff_4_q, not_1_out, not_2_out,
       or_1_out, or_2_out;

  or or_1 (or_1_out, or_2_out, Data);
  Clock clock_1 (.out(clock_1_out));
  D_Flip_Flop d_ff_1 (.D(or_1_out), .clk(clock_1_out), .Q(d_ff_1_q), .preset(Reset));  // open: Qn, reset
  LED led_1 (.in(d_ff_1_q));
  or or_2 (or_2_out, and_1_out, and_2_out);
  and and_1 (and_1_out, OmyJohnson, d_ff_4_q);
  and and_2 (and_2_out, not_1_out, not_2_out);
  D_Flip_Flop d_ff_2 (.D(d_ff_1_q), .clk(clock_1_out), .Q(d_ff_2_q), .reset(Reset));  // open: Qn, preset
  not not_1 (not_1_out, OmyJohnson);
  LED led_2 (.in(d_ff_2_q));
  D_Flip_Flop d_ff_3 (.D(d_ff_2_q), .clk(clock_1_out), .Q(d_ff_3_q), .reset(Reset));  // open: Qn, preset
  not not_2 (not_2_out, d_ff_4_q);
  LED led_3 (.in(d_ff_3_q));
  D_Flip_Flop d_ff_4 (.D(d_ff_3_q), .clk(clock_1_out), .Q(d_ff_4_q), .reset(Reset));  // open: Qn, preset
  LED led_4 (.in(d_ff_4_q));

  // Notes on the sheet:
  //   0 = Johnson counter  1 = ring counter
endmodule
