// Logisim project latch_wStrobe.circ as structural Verilog: 1 circuit, main circuit latch
module latch (
  input  data,
  input  strobe,
  output Q,
  output Qinv
);

  wire RST, transmission_1_p3, TRinv;

  // Transmission_Gate transmission_1: pin names not known; wires that end beside it: strobe, data, transmission_1_p3, TRinv, Qinv
  S_R_Flip_Flop #(.trigger("high")) s_r_ff_1 (
    .S(transmission_1_p3), .R(RST), .clk(strobe), .Q(Q), .Qn(Qinv));  // open: reset, preset
  LED led_1 (.in(transmission_1_p3));
  not not_1 (TRinv, strobe);
  not not_2 (RST, transmission_1_p3);
  LED led_2 (.in(Q));
  LED led_3 (.in(Qinv));
  LED led_4 (.in(RST));

  // Other names for the same wires on the sheet: TR = strobe
endmodule
